// Logisim project CT8.circ as structural Verilog: 9 circuits, main circuit main
module main (
  input  [7:0] in_1,
  input  in_2,
  input  in_3,
  input  [2:0] in_4,
  input  in_5
);

  wire alu_1_cout, alu_1_n, alu_1_saveflag, alu_1_v, alu_1_z, AOE, AWE, C, flagreg_1_cout;
  wire [3:0] Flag;
  wire [7:0] Accumulator_dout, controlled_buffer_1_out;
  wire [15:0] regbank_1_addrbus;

  Clock clock_1 (.out(C));
  assign controlled_buffer_1_out = in_2 ? in_1 : 8'bz;  // Controlled_Buffer controlled_buffer_1
  regs Accumulator (.Din(controlled_buffer_1_out), .WE(AWE), .Clck(C), .OE(AOE), .Dout(Accumulator_dout));  // open: Rst
  regs Temp (.Din(controlled_buffer_1_out), .WE(in_5), .Clck(C), .OE(in_3));  // open: Rst, Dout
  flagReg flagreg_1 (
    .WE(alu_1_saveflag), .Clck(C), .C(alu_1_cout), .N(alu_1_n), .Z(alu_1_z), .V(alu_1_v), .Dout(Flag),
    .Cout(flagreg_1_cout));  // open: Rst
  ALU alu_1 (
    .OP(in_4), .OutEn(in_3), .Cin(flagreg_1_cout), .SaveFlag(alu_1_saveflag),
    .out_7(controlled_buffer_1_out), .COut(alu_1_cout), .Z(alu_1_z), .N(alu_1_n), .V(alu_1_v));  // open: A, B, CEnbl
  // Probe on controlled_buffer_1_out
  instrReg instrreg_1 (.instIn(controlled_buffer_1_out), .Clck(C));  // open: WE, Rst, out_5
  RegBank regbank_1 (
    .Datain(controlled_buffer_1_out), .Awe(AWE), .Aoe(AOE), .DataOut(controlled_buffer_1_out),
    .AddrBus(regbank_1_addrbus));  // open: SEL, Clk, OE, WE, reset

  // Other names for the same wires on the sheet: OE = in_3
endmodule

module ALU (
  input  CEnbl,
  input  Cin,
  input  [7:0] A,
  input  [7:0] B,
  input  [2:0] OP,
  input  OutEn,
  output [7:0] out_7,
  output COut,
  output Z,
  output SaveFlag,
  output N,
  output V
);

  wire adder_1_cout, and_1_out, and_3_out, decoder_1_out0, decoder_1_out2, decoder_1_out3, decoder_1_out4,
       decoder_1_out5, nor_1_out, not_2_out, or_1_out, xor_2_out, xor_4_out, xor_5_out;
  wire [7:0] adder_1_out, and_2_out, controlled_buffer_1_out, not_1_out, or_2_out, xor_1_out, xor_3_out;
  wire [7:7] decoder_1_out1;

  // Probe on A
  // Probe on B
  assign xor_1_out = B ^ {8{decoder_1_out1[7]}};  // XOR_Gate xor_1, 8 bits wide
  Decoder #(.select(3)) decoder_1 (
    .out0(decoder_1_out0), .out1(decoder_1_out1[7]), .out2(decoder_1_out2), .out3(decoder_1_out3),
    .out4(decoder_1_out4), .out5(decoder_1_out5), .sel(OP), .en(1'b1));  // open: out6, out7
  and and_1 (and_1_out, CEnbl, Cin);
  xor xor_2 (xor_2_out, and_1_out, decoder_1_out1[7]);
  or or_1 (or_1_out, decoder_1_out1[7], decoder_1_out0);
  assign controlled_buffer_1_out = or_1_out ? adder_1_out : 8'bz;  // Controlled_Buffer controlled_buffer_1
  Adder adder_1 (.a(A), .b(xor_1_out), .out(adder_1_out), .cin(xor_2_out), .cout(adder_1_cout));
  assign and_2_out = A & xor_1_out;  // AND_Gate and_2, 8 bits wide
  assign controlled_buffer_1_out = decoder_1_out2 ? and_2_out : 8'bz;  // Controlled_Buffer controlled_buffer_2
  assign or_2_out = A | xor_1_out;  // OR_Gate or_2, 8 bits wide
  assign controlled_buffer_1_out = decoder_1_out3 ? or_2_out : 8'bz;  // Controlled_Buffer controlled_buffer_3
  assign xor_3_out = A ^ xor_1_out;  // XOR_Gate xor_3, 8 bits wide
  assign controlled_buffer_1_out = decoder_1_out4 ? xor_3_out : 8'bz;  // Controlled_Buffer controlled_buffer_4
  assign not_1_out = ~A;  // NOT_Gate not_1, 8 bits wide
  assign controlled_buffer_1_out = decoder_1_out5 ? not_1_out : 8'bz;  // Controlled_Buffer controlled_buffer_5
  xor xor_4 (xor_4_out, controlled_buffer_1_out[7], A[7]);
  xor xor_5 (xor_5_out, A[7], B[7]);
  not not_2 (not_2_out, xor_5_out);
  nor nor_1 (nor_1_out, controlled_buffer_1_out[0], controlled_buffer_1_out[1], controlled_buffer_1_out[2], controlled_buffer_1_out[3], controlled_buffer_1_out[4], controlled_buffer_1_out[5], controlled_buffer_1_out[6], controlled_buffer_1_out[7]);
  and and_3 (and_3_out, xor_4_out, not_2_out);
  assign out_7 = OutEn ? controlled_buffer_1_out : 8'bz;  // Controlled_Buffer controlled_buffer_6
  assign COut = OutEn ? adder_1_cout : 1'bz;  // Controlled_Buffer controlled_buffer_7
  assign Z = OutEn ? nor_1_out : 1'bz;  // Controlled_Buffer controlled_buffer_8
  assign N = OutEn ? controlled_buffer_1_out[7] : 1'bz;  // Controlled_Buffer controlled_buffer_9
  assign V = OutEn ? and_3_out : 1'bz;  // Controlled_Buffer controlled_buffer_10
  // Probe on out_7

  assign SaveFlag = OutEn;
endmodule

module regs (
  input  [7:0] Din,
  input  WE,
  input  Clck,
  input  Rst,
  input  OE,
  output [7:0] Dout
);

  wire [7:0] register_1_q;

  Register register_1 (.D(Din), .en(WE), .clk(Clck), .Q(register_1_q), .clr(Rst));
  assign Dout = OE ? register_1_q : 8'bz;  // Controlled_Buffer controlled_buffer_1
endmodule

module instrReg (
  input  [7:0] instIn,
  input  WE,
  input  Clck,
  input  Rst,
  output [7:0] out_5
);

  Register register_1 (.D(instIn), .en(WE), .clk(Clck), .Q(out_5), .clr(Rst));
endmodule

module flagReg (
  input  C,
  input  N,
  input  Z,
  input  V,
  input  WE,
  input  Rst,
  input  Clck,
  output [3:0] Dout,
  output Cout
);

  Register #(.width(4)) register_1 (.D({V, Z, N, C}), .en(WE), .clk(Clck), .Q({Dout[3:1], Cout}), .clr(Rst));

  assign Dout[0] = Cout;
endmodule

module RegBank (
  input  [2:0] SEL,
  input  Clk,
  input  OE,
  input  WE,
  input  [7:0] Datain,
  input  reset,
  output Awe,
  output Aoe,
  output [7:0] DataOut,
  output [15:0] AddrBus
);

  wire decoder_1_out1, decoder_1_out2, decoder_1_out3, decoder_1_out4, decoder_1_out5, decoder_1_out6,
       decoder_2_out1, decoder_2_out2, decoder_2_out3, decoder_2_out4, decoder_2_out5, decoder_2_out6;

  Decoder #(.select(3)) decoder_1 (
    .out0(Awe), .out1(decoder_1_out1), .out2(decoder_1_out2), .out3(decoder_1_out3), .out4(decoder_1_out4),
    .out5(decoder_1_out5), .out6(decoder_1_out6), .sel(SEL), .en(WE));  // open: out7
  regs B (.Din(Datain), .WE(decoder_1_out1), .Clck(Clk), .Rst(reset), .OE(decoder_2_out1), .Dout(DataOut));
  regs D (.Din(Datain), .WE(decoder_1_out3), .Clck(Clk), .Rst(reset), .OE(decoder_2_out3), .Dout(DataOut));
  HLreg hlreg_1 (
    .reset(reset), .DinH(Datain), .clock(Clk), .Hoe(decoder_2_out6), .Loe(decoder_2_out5), .DinL(Datain),
    .Hwe(decoder_1_out6), .Lwe(decoder_1_out5), .H_out(DataOut), .Dout(AddrBus), .L_out(DataOut));
  regs C (.Din(Datain), .WE(decoder_1_out2), .Clck(Clk), .Rst(reset), .OE(decoder_2_out2), .Dout(DataOut));
  regs E (.Din(Datain), .WE(decoder_1_out4), .Clck(Clk), .Rst(reset), .OE(decoder_2_out4), .Dout(DataOut));
  Decoder #(.select(3)) decoder_2 (
    .out0(Aoe), .out1(decoder_2_out1), .out2(decoder_2_out2), .out3(decoder_2_out3), .out4(decoder_2_out4),
    .out5(decoder_2_out5), .out6(decoder_2_out6), .sel(SEL), .en(OE));  // open: out7

  // Other names for the same wires on the sheet: r = reset
endmodule

module PC (
  input  load,
  input  [15:0] AddrBusIn,
  input  CE,
  input  Clock,
  input  Clear,
  output [15:0] AddrBusOut
);

  wire not_1_out;
  wire [15:0] adder_1_out, controlled_buffer_1_out;

  assign controlled_buffer_1_out = load ? AddrBusIn : 16'bz;  // Controlled_Buffer controlled_buffer_1
  Register #(.width(16)) register_1 (.D(controlled_buffer_1_out), .en(CE), .clk(Clock), .Q(AddrBusOut), .clr(Clear));
  not not_1 (not_1_out, load);
  assign controlled_buffer_1_out = not_1_out ? adder_1_out : 16'bz;  // Controlled_Buffer controlled_buffer_2
  Adder #(.width(16)) adder_1 (.a(AddrBusOut), .b(16'h1), .out(adder_1_out), .cin(1'b0));  // open: cout
endmodule

module CLK (
  input  Halt,
  output Rise,
  output Fall,
  output FullClock
);

  wire clock_1_out, not_1_out, not_2_out, not_3_out, not_4_out;

  Clock clock_1 (.out(clock_1_out));
  and and_1 (FullClock, clock_1_out, ~Halt);  // AND_Gate
  not not_1 (not_1_out, FullClock);
  and and_2 (Rise, FullClock, not_1_out);
  not not_2 (not_2_out, FullClock);
  not not_3 (not_3_out, FullClock);
  and and_3 (Fall, not_2_out, not_4_out);
  not not_4 (not_4_out, not_3_out);
endmodule

module HLreg (
  input  [7:0] DinH,
  input  Hoe,
  input  Hwe,
  input  Lwe,
  input  Loe,
  input  clock,
  input  reset,
  input  [7:0] DinL,
  output [7:0] H_out,
  output [15:0] Dout,
  output [7:0] L_out
);

  Register H (.D(DinH), .en(Hwe), .clk(clock), .Q(Dout[15:8]), .clr(reset));
  Register L (.D(DinL), .en(Lwe), .clk(clock), .Q(Dout[7:0]), .clr(reset));
  assign H_out = Hoe ? Dout[15:8] : 8'bz;  // Controlled_Buffer controlled_buffer_1
  assign L_out = Loe ? Dout[7:0] : 8'bz;  // Controlled_Buffer controlled_buffer_2
endmodule
